// Logisim project ALU_8bit.circ as structural Verilog: 5 circuits, main circuit ALU
module AND_8bit (
  input  [7:0] A,
  input  [7:0] B,
  output [7:0] Result_AND
);

  and and_1 (Result_AND[0], A[0], B[0]);
  and and_2 (Result_AND[1], A[1], B[1]);
  and and_3 (Result_AND[2], A[2], B[2]);
  and and_4 (Result_AND[3], A[3], B[3]);
  and and_5 (Result_AND[4], A[4], B[4]);
  and and_6 (Result_AND[5], A[5], B[5]);
  and and_7 (Result_AND[6], A[6], B[6]);
  and and_8 (Result_AND[7], A[7], B[7]);

  // Notes on the sheet:
  //   8-bit AND
endmodule

module OR_8bit (
  input  [7:0] A,
  input  [7:0] B,
  output [7:0] Result_OR
);

  or or_1 (Result_OR[0], A[0], B[0]);
  or or_2 (Result_OR[1], A[1], B[1]);
  or or_3 (Result_OR[2], A[2], B[2]);
  or or_4 (Result_OR[3], A[3], B[3]);
  or or_5 (Result_OR[4], A[4], B[4]);
  or or_6 (Result_OR[5], A[5], B[5]);
  or or_7 (Result_OR[6], A[6], B[6]);
  or or_8 (Result_OR[7], A[7], B[7]);

  // Notes on the sheet:
  //   8-bit OR
endmodule

module Adder_1bit (
  input  C_in,
  input  A,
  input  B,
  output C_out,
  output Sum
);

  wire and_1_out, and_2_out, xor_1_out;

  and and_1 (and_1_out, A, B);
  xor xor_1 (xor_1_out, A, B);
  or or_1 (Sum, and_1_out, and_2_out);
  and and_2 (and_2_out, C_in, xor_1_out);
  xor xor_2 (C_out, C_in, xor_1_out);

  // Notes on the sheet:
  //   FULL ADDER
endmodule

module Add_Sub_8bit (
  input  Add_Sub,
  input  [7:0] A,
  input  [7:0] B,
  output [7:0] SUM,
  output Cout
);

  wire adder_1bit_1_sum, adder_1bit_2_sum, adder_1bit_3_sum, adder_1bit_4_sum, adder_1bit_5_sum,
       adder_1bit_6_sum, adder_1bit_7_sum, xor_1_out, xor_2_out, xor_3_out, xor_4_out, xor_5_out, xor_6_out,
       xor_7_out, xor_8_out;

  xor xor_1 (xor_1_out, Add_Sub, B[0]);
  xor xor_2 (xor_2_out, Add_Sub, B[1]);
  xor xor_3 (xor_3_out, Add_Sub, B[2]);
  xor xor_4 (xor_4_out, Add_Sub, B[3]);
  xor xor_5 (xor_5_out, Add_Sub, B[4]);
  xor xor_6 (xor_6_out, Add_Sub, B[5]);
  xor xor_7 (xor_7_out, Add_Sub, B[6]);
  xor xor_8 (xor_8_out, Add_Sub, B[7]);
  Adder_1bit adder_1bit_1 (.Sum(adder_1bit_1_sum), .B(xor_1_out), .C_in(Add_Sub), .A(A[0]), .C_out(SUM[0]));
  Adder_1bit adder_1bit_2 (.Sum(adder_1bit_2_sum), .B(xor_2_out), .C_in(adder_1bit_1_sum), .A(A[1]), .C_out(SUM[1]));
  Adder_1bit adder_1bit_3 (.Sum(adder_1bit_3_sum), .B(xor_3_out), .C_in(adder_1bit_2_sum), .A(A[2]), .C_out(SUM[2]));
  Adder_1bit adder_1bit_4 (.Sum(adder_1bit_4_sum), .B(xor_4_out), .C_in(adder_1bit_3_sum), .A(A[3]), .C_out(SUM[3]));
  Adder_1bit adder_1bit_5 (.Sum(adder_1bit_5_sum), .B(xor_5_out), .C_in(adder_1bit_4_sum), .A(A[4]), .C_out(SUM[4]));
  Adder_1bit adder_1bit_6 (.Sum(adder_1bit_6_sum), .B(xor_6_out), .C_in(adder_1bit_5_sum), .A(A[5]), .C_out(SUM[5]));
  Adder_1bit adder_1bit_7 (.Sum(adder_1bit_7_sum), .B(xor_7_out), .C_in(adder_1bit_6_sum), .A(A[6]), .C_out(SUM[6]));
  Adder_1bit adder_1bit_8 (.Sum(Cout), .B(xor_8_out), .C_in(adder_1bit_7_sum), .A(A[7]), .C_out(SUM[7]));
endmodule

module ALU (
  input  [7:0] A,
  input  [7:0] B,
  input  [1:0] ALUOUT,
  output [7:0] RESULT
);

  wire [7:0] add_sub_8bit_1_sum, and_8bit_1_result_and, or_8bit_1_result_or;

  AND_8bit and_8bit_1 (.B(B), .A(A), .Result_AND(and_8bit_1_result_and));
  OR_8bit or_8bit_1 (.Result_OR(or_8bit_1_result_or), .A(A), .B(B));
  Add_Sub_8bit add_sub_8bit_1 (.B(B), .SUM(add_sub_8bit_1_sum), .A(A), .Add_Sub(ALUOUT[0]));  // open: Cout
  Multiplexer #(.select(2), .width(8), .enable("false")) multiplexer_1 (
    .in0(and_8bit_1_result_and), .in1(or_8bit_1_result_or), .in2(add_sub_8bit_1_sum),
    .in3(add_sub_8bit_1_sum), .out(RESULT), .sel(ALUOUT));
endmodule
