// Logisim project CPU_8bit.circ as structural Verilog: 13 circuits, main circuit DECODE_LOGIC
module main (
  input  in_1,
  input  in_2,
  output [1:0] out_3,
  output [1:0] out_4,
  output [1:0] out_5,
  output [7:0] Address,
  output [1:0] out_7,
  output [1:0] out_8,
  output [7:0] ALU_out,
  output [1:0] out_10,
  output [7:0] R0,
  output [7:0] R1,
  output [7:0] R2,
  output [7:0] R3,
  output [7:0] out_15,
  output [7:0] data_in,
  output [7:0] data_out
);

  wire and_1_out, clk, d_write, imm_load, ir_load, main_clk, not_1_out, not_2_out, or_1_out, or_2_out,
       pc_load, pc_sel, read_write, register_file_1_neg, register_file_1_zero;
  wire [1:0] counter_1_q, counter_2_q, op1;
  wire [7:0] IMM_q, ir_value, multiplexer_2_out, multiplexer_3_out, pc_adder_1_pc_out, register_1_q, s_bus;

  Clock clock_1 (.out(main_clk));
  Counter #(.width(2), .max('h3)) counter_1 (
    .load(in_2), .clk(or_1_out), .D(2'b10), .Q(counter_1_q));  // open: clr, up, count, carry
  or or_1 (or_1_out, in_2, main_clk);
  Counter #(.width(2), .max('h3)) counter_2 (.clk(main_clk), .Q(counter_2_q));  // open: clr, load, up, count, D, carry
  and and_1 (and_1_out, counter_1_q[1], counter_1_q[0]);
  RAM ram_1 (.addr(Address), .we(read_write), .oe(not_1_out), .clk(or_2_out), .data(out_15));
  not not_1 (not_1_out, read_write);
  or or_2 (or_2_out, and_1_out, clk);
  and and_2 (clk, counter_2_q[0], counter_2_q[1]);
  Multiplexer #(.select(2), .width(8), .enable("false")) multiplexer_1 (
    .in0(register_1_q), .in1(IMM_q), .in2(s_bus), .in3(data_in), .out(Address), .sel(out_7));
  assign out_15 = read_write ? data_in : 8'bz;  // Controlled_Buffer controlled_buffer_1
  assign data_out = not_2_out ? out_15 : 8'bz;  // Controlled_Buffer controlled_buffer_2
  not not_2 (not_2_out, read_write);
  Register IMM (.D(data_out), .en(imm_load), .clk(clk), .Q(IMM_q));  // open: clr
  Register IR (.D(data_out), .en(ir_load), .clk(clk), .Q(ir_value));  // open: clr
  Multiplexer #(.width(8), .enable("false")) multiplexer_2 (
    .in0(IMM_q), .in1(pc_adder_1_pc_out), .out(multiplexer_2_out), .sel(pc_sel));
  PC_ADDER pc_adder_1 (.PC_out(pc_adder_1_pc_out), .PC_in(register_1_q));
  Multiplexer #(.select(2), .width(8), .enable("false")) multiplexer_3 (
    .in0(IMM_q), .in1(s_bus), .in2(data_out), .in3(ALU_out), .out(multiplexer_3_out), .sel(out_10));
  Register register_1 (.D(multiplexer_2_out), .en(pc_load), .clk(clk), .Q(register_1_q), .clr(in_1));
  Phase_counter phase_counter_1 (.in_1(clk), .out_2(out_3));
  REGISTER_FILE register_file_1 (
    .d_bus(data_in), .rd(out_5), .d_write(d_write), .clk(clk), .d_in(multiplexer_3_out), .s_bus(s_bus),
    .rs(out_4), .out_6(R0), .out_7(R1), .out_12(R2), .out_13(R3), .zero(register_file_1_zero),
    .neg(register_file_1_neg));
  CONTROL control_1 (
    .imm_load(imm_load), .op2(out_8), .rd(out_5), .rs(out_4), .zero_flag(register_file_1_zero),
    .neg_flag(register_file_1_neg), .ir_load(ir_load), .read_write(read_write), .op1(op1), .reg_sel(out_10),
    .ir_value(ir_value), .pc_load(pc_load), .addr_sel(out_7), .d_write(d_write), .pc_sel(pc_sel),
    .Phase(out_3));
  ALU alu_1 (.RESULT(ALU_out), .ALUOUT(out_8), .B(s_bus), .A(data_in));

  // Other names for the same wires on the sheet: addr_sel[1:0] = out_7; d_bus[7:0] = data_in; op2[1:0] = out_8;
  //   rd[1:0] = out_5; reg_sel[1:0] = out_10; rs[1:0] = out_4
endmodule

module DECODE_LOGIC (
  input  [7:0] ir_value,
  input  zero_flag,
  input  neg_flag,
  output [1:0] rs,
  output ir_load,
  output [1:0] rd,
  output read_write,
  output [1:0] op2,
  output [1:0] op1,
  output imm_load,
  output [1:0] reg_sel,
  output pc_load,
  output [1:0] addr_sel,
  output d_write
);

  wire and_1_out, and_2_out, and_3_out, and_4_out, multiplexer_1_out, multiplexer_2_out, not_1_out,
       not_2_out, not_3_out, not_4_out, or_1_out;
  wire [1:0] multiplexer_7_out, multiplexer_8_out, PHASE, undriven;

  not not_1 (not_1_out, zero_flag);
  and and_1 (and_1_out, not_1_out, not_2_out);
  not not_2 (not_2_out, neg_flag);
  Multiplexer #(.select(4), .enable("false")) multiplexer_1 (
    .in0(1'b1), .in1(1'b1), .in2(1'b1), .in3(1'b1), .in4(1'b1), .in5(1'b0), .in6(1'b1), .in7(1'b0),
    .in8(1'b0), .in9(1'b0), .in10(1'b0), .in11(1'b0), .in12(1'b1), .in13(1'b0), .in14(1'b1), .in15(1'b0),
    .out(multiplexer_1_out), .sel(ir_value[7:4]));
  not not_3 (not_3_out, ir_value[6]);
  Multiplexer #(.select(2), .enable("false")) multiplexer_2 (
    .in0(zero_flag), .in1(not_1_out), .in2(and_1_out), .in3(neg_flag), .out(multiplexer_2_out),
    .sel(ir_value[5:4]));
  and and_2 (and_2_out, not_3_out, ir_value[7], multiplexer_2_out);
  Multiplexer #(.select(2), .enable("false")) multiplexer_3 (
    .in0(1'b0), .in1(1'b0), .in2(multiplexer_1_out), .in3(1'b0), .out(d_write), .sel(PHASE));
  and and_3 (and_3_out, ir_value[7], ir_value[6], ir_value[4], ir_value[4]);
  Multiplexer #(.select(2), .enable("false")) multiplexer_4 (
    .in0(1'b1), .in1(1'b0), .in2(1'b0), .in3(1'b0), .out(ir_load), .sel(PHASE));
  Multiplexer #(.select(2), .enable("false")) multiplexer_5 (
    .in0(1'b0), .in1(ir_value[7]), .in2(1'b0), .in3(1'b0), .out(imm_load), .sel(PHASE));
  or or_1 (or_1_out, and_2_out, and_3_out);
  Multiplexer #(.select(2), .enable("false")) multiplexer_6 (
    .in0(1'b1), .in1(ir_value[7]), .in2(or_1_out), .in3(1'b0), .out(pc_load), .sel(PHASE));
  not not_4 (not_4_out, ir_value[4]);
  Multiplexer #(.select(4), .width(2), .enable("false")) multiplexer_7 (
    .in0(2'b00), .in1(2'b00), .in2(2'b00), .in3(2'b00), .in4(2'b10), .in5(2'b10), .in6(2'b00), .in7(2'b00),
    .in8(2'b00), .in9(2'b00), .in10(2'b00), .in11(2'b00), .in12(2'b00), .in13(2'b01), .in14(2'b01),
    .in15(2'b00), .out(multiplexer_7_out), .sel(ir_value[7:4]));
  and and_4 (and_4_out, ir_value[4], not_4_out, ir_value[6]);
  Multiplexer #(.select(4), .width(2), .enable("false")) multiplexer_8 (
    .in0(2'b11), .in1(2'b11), .in2(2'b11), .in3(2'b11), .in4(2'b10), .in5(2'b00), .in6(2'b01), .in7(2'b00),
    .in8(2'b00), .in9(2'b00), .in10(2'b00), .in11(2'b00), .in12(2'b10), .in13(2'b00), .in14(2'b00),
    .in15(2'b00), .out(multiplexer_8_out), .sel(ir_value[7:4]));
  Multiplexer #(.select(2), .width(2), .enable("false")) multiplexer_9 (
    .in0(undriven), .in1(undriven), .in2(multiplexer_7_out), .in3(undriven), .out(addr_sel), .sel(PHASE));
  Multiplexer #(.select(2), .enable("false")) multiplexer_10 (
    .in0(1'b0), .in1(1'b0), .in2(and_4_out), .in3(1'b0), .out(read_write), .sel(PHASE));
  Multiplexer #(.select(2), .width(2), .enable("false")) multiplexer_11 (
    .in0(2'b00), .in1(2'b00), .in2(multiplexer_8_out), .in3(2'b00), .out(reg_sel), .sel(PHASE));

  assign op1 = ir_value[7:6];
  assign op2 = ir_value[5:4];
  assign rd = ir_value[3:2];
  assign rs = ir_value[1:0];

  // Other names for the same wires on the sheet: ir_bit6 = ir_value[6]; op1_op2[3:0] = ir_value[7:4];
  //   ir_bit7 = ir_value[7]; ir_bit4 = ir_value[4]; ir_bit5 = ir_value[4]
endmodule

module Phase_counter (
  input  in_1,
  output [1:0] out_2
);

  wire and_1_out;

  Counter #(.width(2), .max('h3)) counter_1 (
    .clr(and_1_out), .clk(in_1), .Q(out_2));  // open: load, up, count, D, carry
  and and_1 (and_1_out, out_2[1], out_2[0]);

  // Other names for the same wires on the sheet: PHASE[1:0] = out_2
endmodule

module IR_LOAD (
);

  wire ir_load;
  wire [1:0] PHASE;

  Multiplexer #(.select(2), .enable("false")) multiplexer_1 (
    .in0(1'b1), .in1(1'b0), .in2(1'b0), .in3(1'b0), .out(ir_load), .sel(PHASE));
endmodule

module IMM_LOAD (
);

  wire imm_load, ir_bit7;
  wire [1:0] PHASE;

  Multiplexer #(.select(2), .enable("false")) multiplexer_1 (
    .in0(1'b0), .in1(ir_bit7), .in2(1'b0), .in3(1'b0), .out(imm_load), .sel(PHASE));
endmodule

module PC_LOAD (
);

  wire and_1_out, and_2_out, and_3_out, ir_bit4, ir_bit5, ir_bit6, ir_bit7, multiplexer_1_out, negative_flag,
       not_1_out, not_2_out, not_3_out, or_1_out, pc_load, zero_flag;
  wire [1:0] op2, PHASE;

  not not_1 (not_1_out, zero_flag);
  and and_1 (and_1_out, not_1_out, not_2_out);
  not not_2 (not_2_out, negative_flag);
  not not_3 (not_3_out, ir_bit6);
  Multiplexer #(.select(2), .enable("false")) multiplexer_1 (
    .in0(zero_flag), .in1(not_1_out), .in2(and_1_out), .in3(negative_flag), .out(multiplexer_1_out), .sel(op2));
  and and_2 (and_2_out, not_3_out, ir_bit7, multiplexer_1_out);
  or or_1 (or_1_out, and_2_out, and_3_out);
  and and_3 (and_3_out, ir_bit7, ir_bit6, ir_bit5, ir_bit4);
  Multiplexer #(.select(2), .enable("false")) multiplexer_2 (
    .in0(1'b1), .in1(ir_bit7), .in2(or_1_out), .in3(1'b0), .out(pc_load), .sel(PHASE));
endmodule

module READ_WRITE (
);

  wire and_1_out, ir_bit4, ir_bit5, ir_bit6, not_1_out, read_write;
  wire [1:0] PHASE;

  not not_1 (not_1_out, ir_bit5);
  and and_1 (and_1_out, ir_bit4, not_1_out, ir_bit6);
  Multiplexer #(.select(2), .enable("false")) multiplexer_1 (
    .in0(1'b0), .in1(1'b0), .in2(and_1_out), .in3(1'b0), .out(read_write), .sel(PHASE));
endmodule

module REGISTER_SELECT (
);

  wire reg_sel;
  wire [1:0] multiplexer_1_out, PHASE, R0, R1, R2, R3;
  wire [3:0] op1_op2;

  Multiplexer #(.select(4), .width(2), .enable("false")) multiplexer_1 (
    .in0(R3), .in1(R3), .in2(R3), .in3(R3), .in4(R2), .in5(R0), .in6(R1), .in7(R0), .in8(R0), .in9(R0),
    .in10(R0), .in11(R0), .in12(R2), .in13(R0), .in14(R0), .in15(R0), .out(multiplexer_1_out), .sel(op1_op2));
  Multiplexer #(.select(2), .enable("false")) multiplexer_2 (
    .in0(1'b0), .in1(1'b0), .in2(multiplexer_1_out[0]), .in3(1'b0), .out(reg_sel), .sel(PHASE));
  // Pins of 1 and 2 bits meet at multiplexer_1_out
endmodule

module DEST_REG_WRITE (
);

  wire d_write, multiplexer_1_out;
  wire [1:0] PHASE;
  wire [3:0] op1_op2;

  Multiplexer #(.select(4), .enable("false")) multiplexer_1 (
    .in0(1'b1), .in1(1'b1), .in2(1'b1), .in3(1'b1), .in4(1'b1), .in5(1'b0), .in6(1'b1), .in7(1'b0),
    .in8(1'b0), .in9(1'b0), .in10(1'b0), .in11(1'b0), .in12(1'b1), .in13(1'b0), .in14(1'b1), .in15(1'b0),
    .out(multiplexer_1_out), .sel(op1_op2));
  Multiplexer #(.select(2), .enable("false")) multiplexer_2 (
    .in0(1'b0), .in1(1'b0), .in2(multiplexer_1_out), .in3(1'b0), .out(d_write), .sel(PHASE));
endmodule

module ADDRESS_SELECT (
);

  wire addr_sel, multiplexer_1_out, R0, R1, R2;
  wire [1:0] PHASE;
  wire [3:0] op1_op2;

  Multiplexer #(.select(4), .enable("false")) multiplexer_1 (
    .in0(R0), .in1(R0), .in2(R0), .in3(R0), .in4(R2), .in5(R2), .in6(R0), .in7(R0), .in8(R0), .in9(R0),
    .in10(R0), .in11(R0), .in12(R0), .in13(R1), .in14(R1), .in15(R0), .out(multiplexer_1_out), .sel(op1_op2));
  Multiplexer #(.select(2), .enable("false")) multiplexer_2 (
    .in0(1'b0), .in1(1'b0), .in2(multiplexer_1_out), .in3(1'b0), .out(addr_sel), .sel(PHASE));
endmodule

module REGISTER_FILE (
  input  d_write,
  input  [1:0] rd,
  input  [7:0] d_in,
  input  [1:0] rs,
  input  clk,
  output [7:0] out_6,
  output [7:0] out_7,
  output [7:0] d_bus,
  output zero,
  output neg,
  output [7:0] s_bus,
  output [7:0] out_12,
  output [7:0] out_13
);

  wire demultiplexer_1_out0, demultiplexer_1_out1, demultiplexer_1_out2, demultiplexer_1_out3;

  Demultiplexer #(.select(2), .enable("false")) demultiplexer_1 (
    .out0(demultiplexer_1_out0), .out1(demultiplexer_1_out1), .out2(demultiplexer_1_out2),
    .out3(demultiplexer_1_out3), .in(d_write), .sel(rd));
  Register R0 (.D(d_in), .en(demultiplexer_1_out0), .clk(clk), .Q(out_6));  // open: clr
  Register R1 (.D(d_in), .en(demultiplexer_1_out1), .clk(clk), .Q(out_7));  // open: clr
  Register R2 (.D(d_in), .en(demultiplexer_1_out2), .clk(clk), .Q(out_12));  // open: clr
  Register R3 (.D(d_in), .en(demultiplexer_1_out3), .clk(clk), .Q(out_13));  // open: clr
  Multiplexer #(.select(2), .width(8), .enable("false")) multiplexer_1 (
    .in0(out_6), .in1(out_7), .in2(out_12), .in3(out_13), .out(d_bus), .sel(rd));
  Multiplexer #(.select(2), .width(8), .enable("false")) multiplexer_2 (
    .in0(out_6), .in1(out_7), .in2(out_12), .in3(out_13), .out(s_bus), .sel(rs));
  nor nor_1 (zero, d_bus[0], d_bus[1], d_bus[2], d_bus[3], d_bus[4], d_bus[5], d_bus[6], d_bus[7]);

  assign neg = d_bus[7];

  // Other names for the same wires on the sheet: negative_flag = d_bus[7]; zero_flag = zero
endmodule

module PC_ADDER (
  input  [7:0] PC_in,
  output [7:0] PC_out
);

  Add_Sub_8bit add_sub_8bit_1 (.B(8'h1), .SUM(PC_out), .A(PC_in), .Add_Sub(1'b0));  // open: Cout
endmodule

module CONTROL (
  input  [7:0] ir_value,
  input  [1:0] Phase,
  input  zero_flag,
  input  neg_flag,
  output [1:0] rs,
  output ir_load,
  output [1:0] rd,
  output read_write,
  output [1:0] op2,
  output [1:0] op1,
  output imm_load,
  output [1:0] reg_sel,
  output pc_load,
  output pc_sel,
  output [1:0] addr_sel,
  output d_write
);

  wire and_1_out, and_2_out, and_3_out, and_4_out, multiplexer_1_out, multiplexer_2_out, not_1_out,
       not_2_out, not_3_out, not_4_out, or_1_out;
  wire [1:0] multiplexer_7_out, multiplexer_8_out;

  not not_1 (not_1_out, zero_flag);
  and and_1 (and_1_out, not_1_out, not_2_out);
  not not_2 (not_2_out, neg_flag);
  Multiplexer #(.select(4), .enable("false")) multiplexer_1 (
    .in0(1'b1), .in1(1'b1), .in2(1'b1), .in3(1'b1), .in4(1'b1), .in5(1'b0), .in6(1'b1), .in7(1'b0),
    .in8(1'b0), .in9(1'b0), .in10(1'b0), .in11(1'b0), .in12(1'b1), .in13(1'b0), .in14(1'b1), .in15(1'b0),
    .out(multiplexer_1_out), .sel(ir_value[7:4]));
  not not_3 (not_3_out, ir_value[6]);
  Multiplexer #(.select(2), .enable("false")) multiplexer_2 (
    .in0(zero_flag), .in1(not_1_out), .in2(and_1_out), .in3(neg_flag), .out(multiplexer_2_out),
    .sel(ir_value[5:4]));
  and and_2 (and_2_out, not_3_out, ir_value[7], multiplexer_2_out);
  Multiplexer #(.select(2), .enable("false")) multiplexer_3 (
    .in0(1'b0), .in1(1'b0), .in2(multiplexer_1_out), .in3(1'b0), .out(d_write), .sel(Phase));
  and and_3 (and_3_out, ir_value[7], ir_value[6], ir_value[5], ir_value[4]);
  Multiplexer #(.select(2), .enable("false")) multiplexer_4 (
    .in0(1'b1), .in1(1'b0), .in2(1'b0), .in3(1'b0), .out(ir_load), .sel(Phase));
  Multiplexer #(.select(2), .enable("false")) multiplexer_5 (
    .in0(1'b0), .in1(ir_value[7]), .in2(1'b0), .in3(1'b0), .out(imm_load), .sel(Phase));
  or or_1 (or_1_out, and_2_out, and_3_out);
  Multiplexer #(.select(2), .enable("false")) multiplexer_6 (
    .in0(1'b1), .in1(ir_value[7]), .in2(or_1_out), .in3(1'b0), .out(pc_load), .sel(Phase));
  not not_4 (not_4_out, ir_value[5]);
  Multiplexer #(.select(4), .width(2), .enable("false")) multiplexer_7 (
    .in0(2'b00), .in1(2'b00), .in2(2'b00), .in3(2'b00), .in4(2'b10), .in5(2'b10), .in6(2'b00), .in7(2'b00),
    .in8(2'b00), .in9(2'b00), .in10(2'b00), .in11(2'b00), .in12(2'b00), .in13(2'b01), .in14(2'b01),
    .in15(2'b00), .out(multiplexer_7_out), .sel(ir_value[7:4]));
  and and_4 (and_4_out, ir_value[4], not_4_out, ir_value[6]);
  Multiplexer #(.select(4), .width(2), .enable("false")) multiplexer_8 (
    .in0(2'b11), .in1(2'b11), .in2(2'b11), .in3(2'b11), .in4(2'b10), .in5(2'b00), .in6(2'b01), .in7(2'b00),
    .in8(2'b00), .in9(2'b00), .in10(2'b00), .in11(2'b00), .in12(2'b10), .in13(2'b00), .in14(2'b00),
    .in15(2'b00), .out(multiplexer_8_out), .sel(ir_value[7:4]));
  Multiplexer #(.select(2), .width(2), .enable("false")) multiplexer_9 (
    .in0(2'b00), .in1(2'b00), .in2(multiplexer_7_out), .in3(2'b00), .out(addr_sel), .sel(Phase));
  Multiplexer #(.select(2), .enable("false")) multiplexer_10 (
    .in0(1'b0), .in1(1'b0), .in2(and_4_out), .in3(1'b0), .out(read_write), .sel(Phase));
  Multiplexer #(.select(2), .enable("false")) multiplexer_11 (
    .in0(1'b1), .in1(1'b1), .in2(1'b0), .in3(1'b0), .out(pc_sel), .sel(Phase));
  Multiplexer #(.select(2), .width(2), .enable("false")) multiplexer_12 (
    .in0(2'b00), .in1(2'b00), .in2(multiplexer_8_out), .in3(2'b00), .out(reg_sel), .sel(Phase));

  assign op1 = ir_value[7:6];
  assign op2 = ir_value[5:4];
  assign rd = ir_value[3:2];
  assign rs = ir_value[1:0];

  // Other names for the same wires on the sheet: ir_bit6 = ir_value[6]; op1_op2[3:0] = ir_value[7:4];
  //   ir_bit7 = ir_value[7]; ir_bit4 = ir_value[4]; ir_bit5 = ir_value[5]
endmodule
